// Logisim project ALU.circ as structural Verilog
module ALU (
  input  [7:0] A,
  input  [7:0] B,
  input  MSB,
  input  in_4,
  input  LSB,
  output [7:0] out_6
);

  wire [7:0] and_1_out, n2_s_compliment_1_out_2, n8_bit_add_1_1_p2, n8_bit_add_1_2_out_2,
       n8_bit_adder_1_out_3, n8_bit_adder_2_out_3, or_1_out;

  assign or_1_out = B | A;  // OR_Gate or_1, 8 bits wide
  assign and_1_out = A & B;  // AND_Gate and_1, 8 bits wide
  _2_s_Compliment u_2_s_compliment_1 (.in_1(B), .out_2(n2_s_compliment_1_out_2));
  _8_bit_adder u_8_bit_adder_1 (.in_1(A), .in_2(n2_s_compliment_1_out_2), .out_3(n8_bit_adder_1_out_3));
  // _8_bit_add_1 8_bit_add_1_1: pin names not known; wires that end beside it: A, n8_bit_add_1_1_p2
  _8_bit_add_1 u_8_bit_add_1_2 (.in_1(B), .out_2(n8_bit_add_1_2_out_2));
  _8_bit_adder u_8_bit_adder_2 (.in_1(A), .in_2(B), .out_3(n8_bit_adder_2_out_3));
  _8_1_MUX u_8_1_mux_1 (
    .in_1(A), .in_2(B), .in_3(n8_bit_add_1_1_p2), .in_4(n8_bit_add_1_2_out_2), .in_5(n8_bit_adder_2_out_3),
    .in_6(n8_bit_adder_1_out_3), .in_7(and_1_out), .in_8(or_1_out), .in_9(MSB), .in_10(in_4), .in_11(LSB),
    .out_12(out_6));

  // Notes on the sheet:
  //   7 6 5 4 3 2 1 0
  //   f2 f1 fo output
  //   0 0 0 a
  //   0 0 1 b
  //   0 1 0 a+1
  //   0 1 1 b+1
  //   1 0 0 a+b
  //   101 a-b
  //   110 a and b
  //   111 a or b
endmodule

module adder (
  input  c_In,
  input  in_1,
  input  in_2,
  output out,
  output c_out
);

  wire and_1_out, and_2_out, and_3_out, and_4_out, and_5_out, and_6_out, and_7_out, not_1_out, not_2_out,
       not_3_out, not_4_out, not_5_out, not_6_out;

  not not_1 (not_1_out, in_2);
  and and_1 (and_1_out, c_In, in_1, not_1_out);
  not not_2 (not_2_out, in_1);
  and and_2 (and_2_out, c_In, not_2_out, in_2);
  not not_3 (not_3_out, c_In);
  not not_4 (not_4_out, in_1);
  not not_5 (not_5_out, in_2);
  not not_6 (not_6_out, c_In);
  and and_3 (and_3_out, in_1, in_2, not_6_out);
  and and_4 (and_4_out, c_In, not_4_out, not_5_out);
  and and_5 (and_5_out, not_3_out, not_4_out, not_4_out, in_2);
  and and_6 (and_6_out, not_3_out, not_5_out, in_1);
  and and_7 (and_7_out, in_2, c_In, in_1);
  or or_1 (c_out, and_3_out, and_2_out, and_7_out, and_1_out);
  or or_2 (out, and_5_out, and_4_out, and_7_out, and_6_out);
endmodule

module adder_no_carry (
  input  in_1,
  input  in_2,
  output out_3,
  output out_4
);

  wire and_2_out, and_3_out, not_1_out, not_2_out;

  and and_1 (out_4, in_2, in_1);
  and and_2 (and_2_out, in_1, not_1_out);
  not not_1 (not_1_out, in_2);
  not not_2 (not_2_out, in_1);
  and and_3 (and_3_out, not_2_out, in_2);
  or or_1 (out_3, and_2_out, and_3_out);
endmodule

module _8_bit_adder (
  input  [7:0] in_1,
  input  [7:0] in_2,
  output [7:0] out_3
);

  wire adder_1_c_out, adder_2_c_out, adder_3_c_out, adder_4_c_out, adder_5_c_out, adder_6_c_out,
       adder_no_carry_1_out_4;

  adder_no_carry adder_no_carry_1 (.in_1(in_1[0]), .in_2(in_2[0]), .out_3(out_3[0]), .out_4(adder_no_carry_1_out_4));
  adder adder_1 (.in_1(in_1[1]), .in_2(in_2[1]), .c_In(adder_no_carry_1_out_4), .c_out(adder_1_c_out), .out(out_3[1]));
  adder adder_2 (.in_1(in_1[2]), .in_2(in_2[2]), .c_In(adder_1_c_out), .c_out(adder_2_c_out), .out(out_3[2]));
  adder adder_3 (.in_1(in_1[3]), .in_2(in_2[3]), .c_In(adder_2_c_out), .c_out(adder_3_c_out), .out(out_3[3]));
  adder adder_4 (.in_1(in_1[4]), .in_2(in_2[4]), .c_In(adder_3_c_out), .c_out(adder_4_c_out), .out(out_3[4]));
  adder adder_5 (.in_1(in_1[5]), .in_2(in_2[5]), .c_In(adder_4_c_out), .c_out(adder_5_c_out), .out(out_3[5]));
  adder adder_6 (.in_1(in_1[6]), .in_2(in_2[6]), .c_In(adder_5_c_out), .c_out(adder_6_c_out), .out(out_3[6]));
  adder adder_7 (.in_1(in_1[7]), .in_2(in_2[7]), .c_In(adder_6_c_out), .out(out_3[7]));  // open: c_out
endmodule

module _8_bit_add_1 (
  input  [7:0] in_1,
  output [7:0] out_2
);

  wire adder_1_c_out, adder_2_c_out, adder_3_c_out, adder_4_c_out, adder_5_c_out, adder_6_c_out,
       adder_no_carry_1_out_4;

  adder_no_carry adder_no_carry_1 (.in_1(in_1[0]), .in_2(1'b1), .out_3(out_2[0]), .out_4(adder_no_carry_1_out_4));
  adder adder_1 (.in_1(in_1[1]), .in_2(1'b0), .c_In(adder_no_carry_1_out_4), .c_out(adder_1_c_out), .out(out_2[1]));
  adder adder_2 (.in_1(in_1[2]), .in_2(1'b0), .c_In(adder_1_c_out), .c_out(adder_2_c_out), .out(out_2[2]));
  adder adder_3 (.in_1(in_1[3]), .in_2(1'b0), .c_In(adder_2_c_out), .c_out(adder_3_c_out), .out(out_2[3]));
  adder adder_4 (.in_1(in_1[4]), .in_2(1'b0), .c_In(adder_3_c_out), .c_out(adder_4_c_out), .out(out_2[4]));
  adder adder_5 (.in_1(in_1[5]), .in_2(1'b0), .c_In(adder_4_c_out), .c_out(adder_5_c_out), .out(out_2[5]));
  adder adder_6 (.in_1(in_1[6]), .in_2(1'b0), .c_In(adder_5_c_out), .c_out(adder_6_c_out), .out(out_2[6]));
  adder adder_7 (.in_1(in_1[7]), .in_2(1'b0), .c_In(adder_6_c_out), .out(out_2[7]));  // open: c_out
endmodule

module _2_1_mux (
  input  [7:0] in_1,
  input  [7:0] in_2,
  input  in_3,
  output [7:0] out_4
);

  wire [7:0] and_1_out, and_2_out, not_1_out;

  assign not_1_out = ~{8{in_3}};  // NOT_Gate not_1, 8 bits wide
  assign and_1_out = {8{in_3}} & in_2;  // AND_Gate and_1, 8 bits wide
  assign and_2_out = in_1 & not_1_out;  // AND_Gate and_2, 8 bits wide
  assign out_4 = and_2_out | and_1_out;  // OR_Gate or_1, 8 bits wide
endmodule

module _4_1_MUX (
  input  [7:0] in_1,
  input  [7:0] in_2,
  input  [7:0] in_3,
  input  [7:0] in_4,
  input  in_5,
  input  in_6,
  output [7:0] out_7
);

  wire [7:0] n2_1_mux_1_out_4, n2_1_mux_2_out_4;

  _2_1_mux u_2_1_mux_1 (.in_1(in_1), .in_2(in_2), .in_3(in_6), .out_4(n2_1_mux_1_out_4));
  _2_1_mux u_2_1_mux_2 (.in_1(in_3), .in_2(in_4), .in_3(in_6), .out_4(n2_1_mux_2_out_4));
  _2_1_mux u_2_1_mux_3 (.in_1(n2_1_mux_1_out_4), .in_2(n2_1_mux_2_out_4), .in_3(in_5), .out_4(out_7));
endmodule

module _8_1_MUX (
  input  [7:0] in_1,
  input  [7:0] in_2,
  input  [7:0] in_3,
  input  [7:0] in_4,
  input  [7:0] in_5,
  input  [7:0] in_6,
  input  [7:0] in_7,
  input  [7:0] in_8,
  input  in_9,
  input  in_10,
  input  in_11,
  output [7:0] out_12
);

  wire [7:0] n4_1_mux_1_out_7, n4_1_mux_2_out_7;

  _4_1_MUX u_4_1_mux_1 (
    .in_1(in_1), .in_2(in_2), .in_3(in_3), .in_4(in_4), .in_5(in_10), .in_6(in_11), .out_7(n4_1_mux_1_out_7));
  _4_1_MUX u_4_1_mux_2 (
    .in_1(in_5), .in_2(in_6), .in_3(in_7), .in_4(in_8), .in_5(in_10), .in_6(in_11), .out_7(n4_1_mux_2_out_7));
  _2_1_mux u_2_1_mux_1 (.in_1(n4_1_mux_1_out_7), .in_2(n4_1_mux_2_out_7), .in_3(in_9), .out_4(out_12));
endmodule

module _2_s_Compliment (
  input  [7:0] in_1,
  output [7:0] out_2
);

  wire [7:0] not_1_out;

  _8_bit_add_1 u_8_bit_add_1_1 (.in_1(not_1_out), .out_2(out_2));
  assign not_1_out = ~in_1;  // NOT_Gate not_1, 8 bits wide
endmodule
